// Logisim project FinalLab.circ as structural Verilog: 10 circuits, main circuit main
module main (
  input  CLR
);

  wire BC_carry, CLK, DWE, SUB, WE;
  wire [1:0] AFS, RSS;
  wire [2:0] AddrA, AddrB, AddrD;
  wire [3:0] multiplexer_1_out, Opcode, undriven_2;
  wire [3:3] Data, three_port_register_1_porta;
  wire [6:0] three_port_register_1_portb;
  wire [7:0] BC_q, undriven;
  wire [7:7] Decoder_data;
  wire [11:7] Prom_data;

  Clock u_CLK (.out(CLK));
  ROM #(.addrWidth(4)) Decoder (.addr(Opcode), .data({Decoder_data[7], SUB, AFS, RSS, DWE, WE}));
  Counter BC (.clr(CLR), .load(CLR), .up(CLK), .count(CLK), .clk(CLK), .D(undriven), .carry(BC_carry), .Q(BC_q));
  ROM #(.dataWidth(16)) Prom (.addr(BC_q), .data({Opcode, Prom_data[11], AddrD, Prom_data[7], AddrA, Data[3], AddrB}));
  Multiplexer #(.select(2), .width(4), .enable("false")) multiplexer_1 (
    .in0({Data[3], AddrB}), .in1(undriven_2),
    .in2({three_port_register_1_porta[3], three_port_register_1_portb[6:4]}), .out(multiplexer_1_out),
    .sel(RSS));  // open: in3
  TTY tty_1 (.data(three_port_register_1_portb), .clk(CLK), .we(DWE), .clr(CLR));
  Three_port_register three_port_register_1 (
    .Datain(multiplexer_1_out), .Addr(AddrD), .WE(WE), .CLK(CLK), .RA_a(AddrA), .RA_b(AddrB),
    .Porta({three_port_register_1_porta[3], three_port_register_1_portb[6:4]}),
    .Portb(three_port_register_1_portb[3:0]));
  ALU alu_1 (
    .A({three_port_register_1_porta[3], three_port_register_1_portb[6:4]}), .O(undriven_2),
    .B(three_port_register_1_portb[3:0]), .S(SUB), .AFS(AFS));

  // Other names for the same wires on the sheet: Data[2:0] = AddrB

  // Notes on the sheet:
  //   contents of Decoder (hex, n*v repeats v):
  //   0 1 9 2 5 15 25 35 7*0 75
  //   contents of Prom (hex, n*v repeats v):
  //   1004 1102 3001 1207 1309 3023 1402 1500 3045 1607 1703 3067 1006 110d 3001 1206 1301 3023 1406 150c
  //   3045 1606 170c 3067 1002 1100 3001 1206 1301 3023 1406 150e 3045 1606 1704 3067 1002 1100 3001 1207
  //   1303 3023 1406 1509 3045 1606 170d 3067 1007 1100 3001 1206 130c 3023 1406 1505 3045 1002 1100 3001
  //   1207 1304 3023 1406 1508 3045 1606 1709 3067 1006 110e 3001 1206 1307 3023 1407 1503 3045 1602 1700
  //   3067 1006 1101 3001 1207 1302 3023 1406 1505 3045 1600 170a 3067 1006 1107 3001 1207 1302 3023 1406
  //   1505 3045 1606 1701 3067 1007 1104 3001 1202 1300 3023 1407 1504 3045 1606 1708 3067 1006 1109 3001
  //   1206 130e 3023 1406 1507 3045 1607 1703 3067 1002 1100 3001 1206 1302 3023 1407 1502 3045 1606 170f
  //   3067 1007 1105 3001 1206 1307 3023 1406 1508 3045 1607 1704 3067 1002 1100 3001 1207 1304 3023 1406
  //   150f 3045 1602 1700 3067 1007 1100 3001 1206 1301 3023 1407 1503 3045 1607 1703 3067 1002 1101 3001
  //   3001 1200 130a 3023 3023
  //   Marshall Haymond
endmodule

module Write_decoder (
  input  Addr_0,
  input  Addr_1,
  input  Addr_2,
  input  Enable,
  output Out_0,
  output Out_1,
  output Out_2,
  output Out_3,
  output Out_4,
  output Out_5,
  output Out_6,
  output Out_7
);

  wire not_1_out, not_2_out, not_3_out;

  not not_1 (not_1_out, Addr_0);
  not not_2 (not_2_out, Addr_1);
  not not_3 (not_3_out, Addr_2);
  and and_1 (Out_0, not_1_out, not_2_out, not_3_out, Enable);
  and and_2 (Out_1, Addr_0, not_2_out, not_3_out, Enable);
  and and_3 (Out_2, not_1_out, Addr_1, not_3_out, Enable);
  and and_4 (Out_3, Addr_0, Addr_1, not_3_out, Enable);
  and and_5 (Out_4, not_1_out, not_2_out, Addr_2, Enable);
  and and_6 (Out_5, Addr_0, not_2_out, Addr_2, Enable);
  and and_7 (Out_6, not_1_out, Addr_1, Addr_2, Enable);
  and and_8 (Out_7, Addr_0, Addr_1, Addr_2, Enable);
endmodule

module Three_port_register (
  input  [3:0] Datain,
  input  [2:0] Addr,
  input  WE,
  input  CLK,
  input  [2:0] RA_a,
  input  [2:0] RA_b,
  output [3:0] Porta,
  output [3:0] Portb
);

  wire write_decoder_1_out_0, write_decoder_1_out_1, write_decoder_1_out_2, write_decoder_1_out_3,
       write_decoder_1_out_4, write_decoder_1_out_5, write_decoder_1_out_6, write_decoder_1_out_7;
  wire [3:0] four_bit_register_1_out_7, four_bit_register_2_out_7, four_bit_register_3_out_7,
       four_bit_register_4_out_7, four_bit_register_5_out_7, four_bit_register_6_out_7,
       four_bit_register_7_out_7, four_bit_register_8_out_7;

  Write_decoder write_decoder_1 (
    .Addr_0(Addr[0]), .Addr_1(Addr[1]), .Addr_2(Addr[2]), .Enable(WE), .Out_0(write_decoder_1_out_0),
    .Out_1(write_decoder_1_out_1), .Out_2(write_decoder_1_out_2), .Out_3(write_decoder_1_out_3),
    .Out_4(write_decoder_1_out_4), .Out_5(write_decoder_1_out_5), .Out_6(write_decoder_1_out_6),
    .Out_7(write_decoder_1_out_7));
  four_bit_register four_bit_register_1 (
    .D0(Datain[0]), .D1(Datain[1]), .D2(Datain[2]), .D3(Datain[3]), .CLK(CLK), .Load(write_decoder_1_out_0),
    .out_7(four_bit_register_1_out_7[0]), .out_8(four_bit_register_1_out_7[1]),
    .out_9(four_bit_register_1_out_7[2]), .out_10(four_bit_register_1_out_7[3]));
  four_bit_register four_bit_register_2 (
    .D0(Datain[0]), .D1(Datain[1]), .D2(Datain[2]), .D3(Datain[3]), .CLK(CLK), .Load(write_decoder_1_out_1),
    .out_7(four_bit_register_2_out_7[0]), .out_8(four_bit_register_2_out_7[1]),
    .out_9(four_bit_register_2_out_7[2]), .out_10(four_bit_register_2_out_7[3]));
  four_bit_register four_bit_register_3 (
    .D0(Datain[0]), .D1(Datain[1]), .D2(Datain[2]), .D3(Datain[3]), .CLK(CLK), .Load(write_decoder_1_out_2),
    .out_7(four_bit_register_3_out_7[0]), .out_8(four_bit_register_3_out_7[1]),
    .out_9(four_bit_register_3_out_7[2]), .out_10(four_bit_register_3_out_7[3]));
  four_bit_register four_bit_register_4 (
    .D0(Datain[0]), .D1(Datain[1]), .D2(Datain[2]), .D3(Datain[3]), .CLK(CLK), .Load(write_decoder_1_out_3),
    .out_7(four_bit_register_4_out_7[0]), .out_8(four_bit_register_4_out_7[1]),
    .out_9(four_bit_register_4_out_7[2]), .out_10(four_bit_register_4_out_7[3]));
  four_bit_register four_bit_register_5 (
    .D0(Datain[0]), .D1(Datain[1]), .D2(Datain[2]), .D3(Datain[3]), .CLK(CLK), .Load(write_decoder_1_out_4),
    .out_7(four_bit_register_5_out_7[0]), .out_8(four_bit_register_5_out_7[1]),
    .out_9(four_bit_register_5_out_7[2]), .out_10(four_bit_register_5_out_7[3]));
  four_bit_register four_bit_register_6 (
    .D0(Datain[0]), .D1(Datain[1]), .D2(Datain[2]), .D3(Datain[3]), .CLK(CLK), .Load(write_decoder_1_out_5),
    .out_7(four_bit_register_6_out_7[0]), .out_8(four_bit_register_6_out_7[1]),
    .out_9(four_bit_register_6_out_7[2]), .out_10(four_bit_register_6_out_7[3]));
  four_bit_register four_bit_register_7 (
    .D0(Datain[0]), .D1(Datain[1]), .D2(Datain[2]), .D3(Datain[3]), .CLK(CLK), .Load(write_decoder_1_out_6),
    .out_7(four_bit_register_7_out_7[0]), .out_8(four_bit_register_7_out_7[1]),
    .out_9(four_bit_register_7_out_7[2]), .out_10(four_bit_register_7_out_7[3]));
  four_bit_register four_bit_register_8 (
    .D0(Datain[0]), .D1(Datain[1]), .D2(Datain[2]), .D3(Datain[3]), .CLK(CLK), .Load(write_decoder_1_out_7),
    .out_7(four_bit_register_8_out_7[0]), .out_8(four_bit_register_8_out_7[1]),
    .out_9(four_bit_register_8_out_7[2]), .out_10(four_bit_register_8_out_7[3]));
  Multiplexer #(.select(3), .width(4), .enable("false")) multiplexer_1 (
    .in0(four_bit_register_1_out_7), .in1(four_bit_register_2_out_7), .in2(four_bit_register_3_out_7),
    .in3(four_bit_register_4_out_7), .in4(four_bit_register_5_out_7), .in5(four_bit_register_6_out_7),
    .in6(four_bit_register_7_out_7), .in7(four_bit_register_8_out_7), .out(Porta), .sel(RA_a));
  Multiplexer #(.select(3), .width(4), .enable("false")) multiplexer_2 (
    .in0(four_bit_register_1_out_7), .in1(four_bit_register_2_out_7), .in2(four_bit_register_3_out_7),
    .in3(four_bit_register_4_out_7), .in4(four_bit_register_5_out_7), .in5(four_bit_register_6_out_7),
    .in6(four_bit_register_7_out_7), .in7(four_bit_register_8_out_7), .out(Portb), .sel(RA_b));
endmodule

module four_bit_register (
  input  D0,
  input  D1,
  input  D2,
  input  D3,
  input  CLK,
  input  Load,
  output out_7,
  output out_8,
  output out_9,
  output out_10
);

  wire multiplexer_1_out, multiplexer_2_out, multiplexer_3_out, multiplexer_4_out;

  Multiplexer #(.enable("false")) multiplexer_1 (.in0(out_7), .in1(D0), .out(multiplexer_1_out), .sel(Load));
  Multiplexer #(.enable("false")) multiplexer_2 (.in0(out_8), .in1(D1), .out(multiplexer_2_out), .sel(Load));
  Multiplexer #(.enable("false")) multiplexer_3 (.in0(out_9), .in1(D2), .out(multiplexer_3_out), .sel(Load));
  Multiplexer #(.enable("false")) multiplexer_4 (.in0(out_10), .in1(D3), .out(multiplexer_4_out), .sel(Load));
  D_Flip_Flop d_ff_1 (.D(multiplexer_1_out), .clk(CLK), .Q(out_7));  // open: Qn, preset, reset
  D_Flip_Flop d_ff_2 (.D(multiplexer_2_out), .clk(CLK), .Q(out_8));  // open: Qn, preset, reset
  D_Flip_Flop d_ff_3 (.D(multiplexer_3_out), .clk(CLK), .Q(out_9));  // open: Qn, preset, reset
  D_Flip_Flop d_ff_4 (.D(multiplexer_4_out), .clk(CLK), .Q(out_10));  // open: Qn, preset, reset
endmodule

module ALU_XOR (
  input  [3:0] A,
  input  [3:0] O,
  input  [3:0] B
);

  xor xor_1 (O[0], A[0], B[0]);
  xor xor_2 (O[1], A[1], B[1]);
  xor xor_3 (O[2], A[2], B[2]);
  xor xor_4 (O[3], A[3], B[3]);
endmodule

module ALU_AND (
  input  [3:0] A,
  input  [3:0] O,
  input  [3:0] B
);

  and and_1 (O[0], A[0], B[0]);
  and and_2 (O[1], A[1], B[1]);
  and and_3 (O[2], A[2], B[2]);
  and and_4 (O[3], A[3], B[3]);
endmodule

module ALU_OR (
  input  [3:0] A,
  input  [3:0] O,
  input  [3:0] B
);

  or or_1 (O[0], A[0], B[0]);
  or or_2 (O[1], A[1], B[1]);
  or or_3 (O[2], A[2], B[2]);
  or or_4 (O[3], A[3], B[3]);
endmodule

module ALU_4ADD (
  input  [3:0] A,
  input  [3:0] O,
  input  [3:0] B,
  input  CIN
);

  wire alu_1add_1_cout, alu_1add_2_cout, alu_1add_3_cout, xor_1_out, xor_2_out, xor_3_out, xor_4_out;

  xor xor_1 (xor_1_out, CIN, B[0]);
  xor xor_2 (xor_2_out, CIN, B[1]);
  xor xor_3 (xor_3_out, CIN, B[2]);
  xor xor_4 (xor_4_out, CIN, B[3]);
  ALU_1ADD alu_1add_1 (.A(A[0]), .B(xor_1_out), .CIN(CIN), .S(O[0]), .COUT(alu_1add_1_cout));
  ALU_1ADD alu_1add_2 (.A(A[1]), .B(xor_2_out), .CIN(alu_1add_1_cout), .S(O[1]), .COUT(alu_1add_2_cout));
  ALU_1ADD alu_1add_3 (.A(A[2]), .B(xor_3_out), .CIN(alu_1add_2_cout), .S(O[2]), .COUT(alu_1add_3_cout));
  ALU_1ADD alu_1add_4 (.A(A[3]), .B(xor_4_out), .CIN(alu_1add_3_cout), .S(O[3]));  // open: COUT
endmodule

module ALU_1ADD (
  input  A,
  input  B,
  input  CIN,
  output S,
  output COUT
);

  wire and_1_out, and_2_out;

  xor xor_1 (S, A, B);
  and and_1 (and_1_out, B, A);
  and and_2 (and_2_out, S, CIN);
  or or_1 (COUT, and_2_out, and_1_out);
endmodule

module ALU (
  input  [3:0] A,
  input  [3:0] O,
  input  [3:0] B,
  input  S,
  input  [1:0] AFS
);

  wire [3:0] undriven, undriven_2, undriven_3, undriven_4;

  ALU_XOR alu_xor_1 (.A(A), .O(undriven), .B(B));
  ALU_AND alu_and_1 (.A(A), .O(undriven_4), .B(B));
  ALU_OR alu_or_1 (.A(A), .O(undriven_3), .B(B));
  ALU_4ADD alu_4add_1 (.A(A), .O(undriven_2), .B(B), .CIN(S));
  Multiplexer #(.select(2), .width(4), .enable("false")) multiplexer_1 (
    .in0(undriven), .in1(undriven_4), .in2(undriven_3), .in3(undriven_2), .out(O), .sel(AFS));
endmodule
